# Fritzing sketch Turnstile (saved by Fritzing 0.9.3b)

parts:
  U1 = ESP8266 NodeMCU LoLin module
  S4 = Pushbutton [package="[THT]"]
  LCD2 = LCD screen
  LCM1602_IIC2 = LCM1602 IIC [part_number="LCM1602 IIC" chip_label="LCM1602 IIC" package="DIP (Dual Inline) [THT]"]
  S5 = Pushbutton [package="[THT]"]
  S6 = Pushbutton [package="[THT]"]
  S7 = Pushbutton [package="[THT]"]
  R1 = Resistor [tolerance=±5% resistance=10k package=THT]
  R2 = Resistor [tolerance=±5% resistance=10k package=THT]
  R3 = Resistor [tolerance=±5% resistance=10k package=THT]
  R4 = Resistor [tolerance=±5% resistance=10k package=THT]

nets:
  N1: U1.D0, S5.Pin_3, S5.Pin_4, R2.Pin_0
  N2: U1.D1, LCM1602_IIC2.SCL
  N3: U1.D2, LCM1602_IIC2.SDA
  N4: U1.3V3, S4.Pin_1, S4.Pin_2, S5.Pin_1, S5.Pin_2, S6.Pin_1, S6.Pin_2, S7.Pin_1, S7.Pin_2
  N5: U1.D6, S7.Pin_3, S7.Pin_4, R4.Pin_0
  N6: U1.D7, S4.Pin_3, S4.Pin_4, R1.Pin_0
  N7: U1.D8, S6.Pin_3, S6.Pin_4, R3.Pin_0
  GND: U1.GND, LCM1602_IIC2.GND, R1.Pin_1, R2.Pin_1, R3.Pin_1, R4.Pin_1
  VIN: U1.Vin, LCM1602_IIC2.VCC
  VSS: LCD2.VSS, LCM1602_IIC2.VSS
  VDD: LCD2.VDD, LCM1602_IIC2.VDD
  N8: LCD2.V0, LCM1602_IIC2.V0
  N9: LCD2.RS, LCM1602_IIC2.RS
  N10: LCD2.R/W, LCM1602_IIC2.RW
  N11: LCD2.E, LCM1602_IIC2.E
  N12: LCD2.DB0, LCM1602_IIC2.D0
  N13: LCD2.DB1, LCM1602_IIC2.D1
  N14: LCD2.DB2, LCM1602_IIC2.D2
  N15: LCD2.DB3, LCM1602_IIC2.D3
  N16: LCD2.DB4, LCM1602_IIC2.D4
  N17: LCD2.DB5, LCM1602_IIC2.D5
  N18: LCD2.DB6, LCM1602_IIC2.D6
  N19: LCD2.DB7, LCM1602_IIC2.D7
  N20: LCD2.LED+, LCM1602_IIC2.A
  N21: LCD2.LED-, LCM1602_IIC2.K
  N22: LCM1602_IIC2.LED_A, LCM1602_IIC2.LED_B

custom parts:
  ESP8266 NodeMCU LoLin module: ESP8266 based NodeMCU
  LCM1602 IIC: I2C-Module to use a 1602 or 2004 LCD on with the wire.h libory Serial LCD Modul
