# Fritzing sketch Turnstile_NoLCD (saved by Fritzing 0.9.3b)

parts:
  U1 = ESP8266 NodeMCU LoLin module
  S4 = Pushbutton [package="[THT]"]
  LCM1602_IIC2 = LCM1602 IIC [part_number="LCM1602 IIC" chip_label="LCM1602 IIC" package="DIP (Dual Inline) [THT]"]
  S5 = Pushbutton [package="[THT]"]
  S6 = Pushbutton [package="[THT]"]
  S7 = Pushbutton [package="[THT]"]
  R1 = Resistor [tolerance=±5% resistance=10k package=THT]
  R2 = Resistor [tolerance=±5% resistance=10k package=THT]
  R3 = Resistor [tolerance=±5% resistance=10k package=THT]
  R4 = Resistor [tolerance=±5% resistance=10k package=THT]

nets:
  N1: U1.D0, S5.Pin_3, S5.Pin_4, R2.Pin_0
  N2: U1.D1, LCM1602_IIC2.SCL
  N3: U1.D2, LCM1602_IIC2.SDA
  N4: U1.D6, S7.Pin_3, S7.Pin_4, R4.Pin_0
  N5: U1.D7, S4.Pin_3, S4.Pin_4, R1.Pin_0
  N6: U1.D8, S6.Pin_3, S6.Pin_4, R3.Pin_0
  GND: U1.GND, LCM1602_IIC2.GND, R1.Pin_1, R2.Pin_1, R3.Pin_1, R4.Pin_1
  N7: U1.3V3, S4.Pin_1, S4.Pin_2, S5.Pin_1, S5.Pin_2, S6.Pin_1, S6.Pin_2, S7.Pin_1, S7.Pin_2
  VIN: U1.Vin, LCM1602_IIC2.VCC
  N8: LCM1602_IIC2.LED_A, LCM1602_IIC2.LED_B

custom parts:
  ESP8266 NodeMCU LoLin module: ESP8266 based NodeMCU
  LCM1602 IIC: I2C-Module to use a 1602 or 2004 LCD on with the wire.h libory Serial LCD Modul
